// Logisim project 2_1.circ as structural Verilog
module lab1 (
  input  x1,
  input  x2,
  input  x3,
  input  x4,
  output y
);

  wire not_1_out, not_2_out, not_3_out, not_4_out, not_5_out, not_6_out, not_7_out, not_8_out, or_1_out,
       or_2_out, or_3_out, or_4_out;

  not not_1 (not_1_out, x4);
  not not_2 (not_2_out, x3);
  not not_3 (not_3_out, x4);
  not not_4 (not_4_out, x2);
  not not_5 (not_5_out, x4);
  not not_6 (not_6_out, x1);
  not not_7 (not_7_out, x2);
  not not_8 (not_8_out, x3);
  or or_1 (or_1_out, x1, not_1_out);
  or or_2 (or_2_out, x2, not_2_out, not_3_out);
  or or_3 (or_3_out, not_4_out, x3, not_5_out);
  or or_4 (or_4_out, not_6_out, not_7_out, not_8_out, x4);
  and and_1 (y, or_1_out, or_2_out, or_3_out, or_4_out);
endmodule
