// Logisim project lab2.circ as structural Verilog
module lab2_1 (
  input  x1,
  input  x2,
  input  x3,
  input  x4,
  output y
);

  wire and_1_out, and_2_out, and_3_out, and_4_out, not_1_out, not_2_out, not_3_out, not_4_out, not_5_out,
       not_6_out, not_7_out;

  not not_1 (not_1_out, x1);
  not not_2 (not_2_out, x2);
  not not_3 (not_3_out, x3);
  not not_4 (not_4_out, x4);
  not not_5 (not_5_out, x2);
  not not_6 (not_6_out, x1);
  not not_7 (not_7_out, x4);
  and and_1 (and_1_out, not_1_out, not_2_out, not_3_out, not_4_out);
  and and_2 (and_2_out, not_5_out, x3, x4);
  and and_3 (and_3_out, not_6_out, x2, x4);
  and and_4 (and_4_out, x1, x2, not_7_out);
  or or_1 (y, and_1_out, and_2_out, and_3_out, and_4_out);
endmodule

module lab2_2 (
  input  x1,
  input  x2,
  input  x3,
  input  x4,
  output y
);

  wire not_1_out, not_2_out, not_3_out, not_4_out, not_5_out, not_6_out, not_7_out, or_1_out, or_2_out,
       or_3_out, or_4_out;

  not not_1 (not_1_out, x4);
  not not_2 (not_2_out, x3);
  not not_3 (not_3_out, x4);
  not not_4 (not_4_out, x2);
  not not_5 (not_5_out, x1);
  not not_6 (not_6_out, x2);
  not not_7 (not_7_out, x4);
  or or_1 (or_1_out, x1, x2, not_1_out);
  or or_2 (or_2_out, not_2_out, not_3_out);
  or or_3 (or_3_out, x1, not_4_out, x3, x4);
  or or_4 (or_4_out, not_5_out, not_6_out, not_7_out);
  and and_1 (y, or_1_out, or_2_out, or_3_out, or_4_out);
endmodule
